# Fritzing sketch arduino-proto-03-tres-ledes (saved by Fritzing 0.9.4)
breadboards: 1

parts:
  Arduino_UNO = Arduino Uno (Rev3)
  LED1 = LED - 5mm [color="Green (570nm)" package="5 mm [THT]"]
  R1 = Resistor [tolerance=±5% resistance=220 package=THT]
  R2 = Resistor [tolerance=±5% resistance=220 package=THT]
  LED2 = LED - 5mm [color="Orange (620nm)" package="5 mm [THT]"]
  R3 = Resistor [tolerance=±5% resistance=220 package=THT]
  LED3 = LED - 5mm [color="Red (633nm)" package="5 mm [THT]"]

nets:
  N1: Arduino_UNO.GND, LED1.cathode, LED2.cathode, LED3.cathode
  N2: Arduino_UNO.D2, R1.Pin_0
  N3: Arduino_UNO.D3_PWM, R2.Pin_0
  N4: Arduino_UNO.D4, R3.Pin_0
  N5: LED1.anode, R1.Pin_1
  N6: R2.Pin_1, LED2.anode
  N7: R3.Pin_1, LED3.anode
