# Fritzing sketch arduino-proto-04-push-ledes (saved by Fritzing 0.9.4)
breadboards: 1

parts:
  LED1 = LED - 5mm [color="Green (570nm)" package="5 mm [THT]"]
  R1 = Resistor [tolerance=±5% resistance=220 package=THT]
  R2 = Resistor [tolerance=±5% resistance=220 package=THT]
  LED3 = LED - 5mm [color="Red (633nm)" package="5 mm [THT]"]
  Arduino_UNO = Arduino Uno (Rev3)
  S1 = Pushbutton [package="[THT]"]
  S2 = Pushbutton [package="[THT]"]

nets:
  N1: LED1.cathode, LED3.cathode, Arduino_UNO.GND, S1.Pin_1, S1.Pin_2, S2.Pin_1, S2.Pin_2
  N2: LED1.anode, R1.Pin_1
  N3: R1.Pin_0, Arduino_UNO.D2
  N4: R2.Pin_0, Arduino_UNO.D3_PWM
  N5: R2.Pin_1, LED3.anode
  N6: Arduino_UNO.D8, S1.Pin_3, S1.Pin_4
  N7: Arduino_UNO.D9_PWM, S2.Pin_3, S2.Pin_4
