# Fritzing sketch arduino-proto-05-pot (saved by Fritzing 0.9.4)
breadboards: 1

parts:
  Arduino_UNO = Arduino Uno (Rev3)
  LED1 = LED - 5mm [color="Green (570nm)" package="5 mm [THT]"]
  R1 = Resistor [tolerance=±5% resistance=220 package=THT]
  R2 = Resistor [tolerance=±5% resistance=220 package=THT]
  LED2 = LED - 5mm [color="Red (660nm)" package="5 mm [THT]"]
  R4 = Rotary Potentiometer (Large) [maximum_resistance=10kΩ package=THT]

nets:
  N1: Arduino_UNO.A0, R4.wiper
  N2: Arduino_UNO.GND, LED1.cathode, LED2.cathode, R4.leg1
  N3: Arduino_UNO.D3_PWM, R1.Pin_0
  N4: Arduino_UNO.D5_PWM, R2.Pin_0
  N5: Arduino_UNO.5V, R4.leg2
  N6: LED1.anode, R1.Pin_1
  N7: R2.Pin_1, LED2.anode
