# Fritzing sketch arduino-proto-06-buzzer (saved by Fritzing 0.9.4)
breadboards: 1

parts:
  R1 = Resistor [tolerance=±5% resistance=220 package=THT]
  J1 = Piezo Speaker
  S1 = Pushbutton [package="[THT]"]
  Arduino_UNO = Arduino Uno (Rev3)

nets (from the schematic view):
  N1: R1.Pin_0, Arduino_UNO.D3_PWM
  N2: R1.Pin_1, J1.pin1
  N3: J1.pin2, S1.Pin_1, S1.Pin_2, Arduino_UNO.GND
  N4: S1.Pin_3, S1.Pin_4, Arduino_UNO.D7
