# Fritzing sketch arduino-proto-01-led-vcc (saved by Fritzing 0.9.4)
breadboards: 1

parts:
  Arduino_UNO = Arduino Uno (Rev3)
  R1 = Resistor [tolerance=±5% resistance=220 package=THT]
  LED1 = LED - 5mm [color="Red (633nm)" package="5 mm [THT]"]

nets:
  N1: Arduino_UNO.5V, R1.Pin_0
  N2: Arduino_UNO.GND, LED1.cathode
  N3: R1.Pin_1, LED1.anode
