# Fritzing sketch arduino-proto-02-led-d2 (saved by Fritzing 0.9.4)
breadboards: 1

parts:
  Arduino_UNO = Arduino Uno (Rev3)
  LED1 = LED - 5mm [color="Red (633nm)" package="5 mm [THT]"]
  R1 = Resistor [tolerance=±5% resistance=220 package=THT]

nets:
  N1: Arduino_UNO.GND, LED1.cathode
  N2: Arduino_UNO.D2, R1.Pin_0
  N3: LED1.anode, R1.Pin_1
