# Fritzing sketch arduino-proto-07-ldr (saved by Fritzing 0.9.4)
breadboards: 1

parts:
  Arduino_UNO = Arduino Uno (Rev3)
  R1 = Resistor [tolerance=±5% resistance=220 package=THT]
  R2 = Resistor [tolerance=±5% resistance=220 package=THT]
  R5 = Photocell (LDR) [package=THT]
  LED1 = RGB LED - (4 legs) [package="5 mm [THT]"]
  R3 = Resistor [tolerance=±5% resistance=220 package=THT]

nets:
  N1: Arduino_UNO.A0, R5.pin_1
  N2: Arduino_UNO.D9_PWM, R3.Pin_0
  N3: Arduino_UNO.GND, R5.pin_0
  N4: Arduino_UNO.D5_PWM, R1.Pin_0
  N5: Arduino_UNO.D6_PWM, R2.Pin_0
  N6: Arduino_UNO.5V, LED1.common_anode
  N7: R1.Pin_1, LED1.blue_cathode
  N8: R2.Pin_1, LED1.green_cathode
  N9: LED1.red_cathode, R3.Pin_1
