# Fritzing sketch ardu-conduct-meter (saved by Fritzing 0.9.4)
breadboards: 1

parts:
  Sensor_Humedad = Soil Moisture Sensor
  Arduino_UNO = Arduino Uno (Rev3)
  R1 = Resistor [tolerance=±1% resistance=10k package=THT]
  LCD_Serial = LCD screen
  C1 = Ceramic Capacitor [capacitance=100nF voltage=50V package="100 mil [THT, multilayer]"]

nets:
  N1: Sensor_Humedad.GND, Arduino_UNO.A2
  N2: Sensor_Humedad.VCC, Arduino_UNO.A1, R1.Pin_0, C1.0
  N3: Arduino_UNO.A0, R1.Pin_1, C1.1
  N4: Arduino_UNO.A4/SDA, LCD_Serial.V0
  N5: Arduino_UNO.A5/SCL, LCD_Serial.RS
  GND: Arduino_UNO.GND, LCD_Serial.VSS
  5V: Arduino_UNO.5V, LCD_Serial.VDD

notes:
  LCD Serial
